// Logisim project conversor_7segmentos.circ as structural Verilog: 1 circuit, main circuit main
module main (
  input  A,
  input  B,
  input  C,
  output out_4,
  output out_5,
  output out_6,
  output out_7,
  output out_8,
  output out_9,
  output out_10
);

  segmento_a_main main_1 (.A(A), .B(B), .C(C), .out_4(out_4));
  segmento_b_main main_2 (.A(A), .B(B), .C(C), .out_4(out_5));
  segmento_c_main main_3 (.A(A), .B(B), .C(C), .out_4(out_6));
  segmento_d_main main_4 (.A(A), .B(B), .C(C), .out_4(out_7));
  segmento_e_main main_5 (.in_1(A), .in_2(B), .in_3(C), .out_4(out_8));
  segmento_f_main main_6 (.A(A), .B(B), .C(C), .out_4(out_9));
  segmento_g_main main_7 (.A(A), .B(B), .C(C), .out_4(out_10));
endmodule
