// Logisim project full_adder.circ as structural Verilog: 1 circuit, main circuit main
module main (
  input  a,
  input  b,
  input  ci,
  output s,
  output out_5
);

  wire and_1_out, and_2_out, xor_1_out;

  xor xor_1 (xor_1_out, a, b);
  xor xor_2 (s, xor_1_out, ci);
  and and_1 (and_1_out, ci, xor_1_out);
  or or_1 (out_5, and_1_out, and_2_out);
  and and_2 (and_2_out, b, a);
endmodule
