// Logisim project registrador_3bits.circ as structural Verilog: 1 circuit, main circuit main
module main (
  input  in_1,
  input  in_2,
  input  in_3,
  output out_4,
  output out_5,
  output out_6
);

  wire clock_1_out;

  Clock clock_1 (.out(clock_1_out));
  D_Flip_Flop _2 (.clk(clock_1_out), .D(in_1), .Q(out_4));  // open: Qn, preset, en, reset
  D_Flip_Flop _1 (.clk(clock_1_out), .D(in_2), .Q(out_5));  // open: Qn, preset, en, reset
  D_Flip_Flop _0 (.clk(clock_1_out), .D(in_3), .Q(out_6));  // open: Qn, preset, en, reset
endmodule
