// Logisim project somador_3bits.circ as structural Verilog: 1 circuit, main circuit main
module main (
  input  a2,
  input  b2,
  input  a1,
  input  b1,
  input  a0,
  input  b0,
  output out_7,
  output out_8,
  output out_9,
  output out_10
);

  wire main_2_out_5, main_3_out_3;

  full_adder_main main_1 (.a(a2), .b(b2), .ci(main_2_out_5), .s(out_8), .out_5(out_7));
  full_adder_main main_2 (.a(a1), .b(b1), .ci(main_3_out_3), .s(out_9), .out_5(main_2_out_5));
  half_adder_main main_3 (.in_1(a0), .in_2(b0), .out_3(main_3_out_3), .out_4(out_10));
endmodule
